# Fritzing sketch schema (saved by Fritzing 1.0.4)
breadboards: 1

parts:
  Air_valve_(24_V_18_5_W) = Solenoid
  24_V = Power plug
  Atmospheric_valve_(24_V_18_5_W) = Solenoid
  Optocoupler = Sharp PC817 [package=THT]
  Pressure_valve_(24_V_18_5_W) = Solenoid
  Optocoupler_2 = Sharp PC817 [package=THT]
  Optocoupler_3 = Sharp PC817 [package=THT]
  J4 = screw terminal, 4 pins
  J5 = screw terminal, 4 pins
  Lower_sensor = Pushbutton [package="[THT]"]
  Higher_sensor = Pushbutton [package="[THT]"]
  Part1 = Arduino Uno (Rev3) - ICSP

nets:
  N1: Air_valve_(24_V_18_5_W).pin1, Optocoupler_3.Pin_3
  N2: Air_valve_(24_V_18_5_W).pin2, J4.pin2
  N3: 24_V.GND, J5.pin1
  N4: 24_V.VCC, J4.pin1
  N5: Atmospheric_valve_(24_V_18_5_W).pin1, Optocoupler.Pin_3
  N6: Atmospheric_valve_(24_V_18_5_W).pin2, J4.pin4
  N7: Optocoupler.Pin_1, Part1.D2
  N8: Optocoupler.Pin_2, Optocoupler_2.Pin_2, Optocoupler_3.Pin_2, Lower_sensor.Pin_1, Lower_sensor.Pin_2, Higher_sensor.Pin_1, Higher_sensor.Pin_2, Part1.GND
  N9: Optocoupler.Pin_4, J5.pin3
  N10: Pressure_valve_(24_V_18_5_W).pin1, Optocoupler_2.Pin_3
  N11: Pressure_valve_(24_V_18_5_W).pin2, J4.pin3
  N12: Optocoupler_2.Pin_1, Part1.D3_PWM
  N13: Optocoupler_2.Pin_4, J5.pin2
  N14: Optocoupler_3.Pin_1, Part1.D4
  N15: Optocoupler_3.Pin_4, J5.pin4
  N16: Lower_sensor.Pin_3, Lower_sensor.Pin_4, Part1.D6_PWM
  N17: Higher_sensor.Pin_3, Higher_sensor.Pin_4, Part1.D5_PWM
